# Fritzing sketch PortableServo (saved by Fritzing 0.9.3b)
breadboards: 1

parts:
  Part1 = Arduino Uno (Rev3)  # not connected
  Part2 = Prototyping Shield
  VCC1 = Battery block 9V
  J1 = Basic Servo
  R1 = Resistor [tolerance=±5% resistance=10k package=THT]
  R2 = Resistor [tolerance=±5% resistance=10k package=THT]
  S3 = Round Pushbutton
  S5 = Round Pushbutton

nets:
  N1: Part2.D9_PWM, J1.pulse
  N2: Part2.D11_PWM/MOSI, R2.Pin_0, S3.leg1
  N3: Part2.D12/MISO, R1.Pin_0, S5.leg1
  N4: Part2.GND#89, VCC1.-
  N5: Part2.VIN, VCC1.+
  N6: Part2.5V#94, S3.leg0
  N7: Part2.5V#95, S5.leg0
  N8: Part2.5V#96, J1.vcc
  N9: Part2.GND#97, J1.gnd
  N10: Part2.GND#98, R2.Pin_1
  N11: Part2.GND#101, R1.Pin_1

custom parts:
  Prototyping Shield: The Arduino Uno is a microcontroller board based on the ATmega328 (datasheet). It has 14 digital input/output pins (of which 6 can be used as PWM outputs), 6 analog inputs, a 16 MHz ceramic resonator, a USB connection, a power jack, an ICSP header, and a reset button. It contains everything needed to support the microcontroller; simply connect it to a computer with a USB cable or power it with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
